# Fritzing sketch PiPower HAT (saved by Fritzing 0.9.3b)
circuit board: 6.52541cm x 5.62539cm
breadboards: 1

parts:
  JACK2 = 2.1mm DC Barrel Jack  # not connected
  JACK1 = USB_AB [package=usb-ab-micro-smd]
  J1 = Cobbler Plus Cable
  Button = male pin header, 4 pins [form="♂ (male)"]
  Arduino = Arduino Pro Mini (5V)
  U1 = MOSFET - HEXFET - IRF7319 [part_number=IRF7319PbF package=so08]
  LED1 = smd LED [color="Green (560nm)" package="1206 [SMD]"]
  R1 = Resistor [tolerance=±5% resistance=100 package="1206 [SMD]"]

nets:
  GND: JACK1.GND, J1.GND#8, J1.GND#24, J1.GND#38, Button.pin2, Button.pin3, Arduino.GND, LED1.cathode
  N1: JACK1.VBUS, Arduino.RAW, R1.Pin_1
  N2: J1.5.0V#1, U1.D1
  N3: J1.TXD, Arduino.RXI
  N4: J1.RXD, Arduino.TXO
  N5: Button.pin1, Arduino.SCK
  N6: Button.pin4, Arduino.D3
  N7: Arduino.VCC, U1.S1
  N8: Arduino.D10, U1.G1
  N9: LED1.anode, R1.Pin_0

notes:
  + -  - +

custom parts:
  2.1mm DC Barrel Jack: 2.1mm DC Barrel Jack with Thru-Hole Connectors (breadboardable)
  Cobbler Plus Cable: The Cobbler Plus is an add on prototyping board from Adafruit specifically designed for the Raspberry Pi B+ that can break out all those tasty power, GPIO, I2C and SPI pins from the 40-pin header onto a solderless breadboard. This set will make "cobbling together" prototypes with the Pi super easy. The Cobbler Plus can plug into any solderless breadboard.
  MOSFET - HEXFET - IRF7319: International Rectifier IRF7319PbF
